// Logisim project Latch Tests.circ as structural Verilog: 2 circuits, main circuit main
module main (
  input  in_1,
  input  in_2,
  input  in_3,
  input  in_4
);

  wire clock_1_out, clock_2_out, d_ff_1_q, d_ff_1_qn, d_ff_2_q, d_ff_2_qn, nand_1_out, nand_2_out,
       nand_3_out, nand_4_out, nand_5_out, nand_6_out, nand_7_out, nand_8_out, nand_9_out, nand_10_out,
       nand_11_out, nand_12_out, nand_13_out, nand_14_out, nand_15_out, nand_16_out, nand_17_out,
       nand_18_out, nand_19_out, nand_20_out, nand_21_out, nand_22_out, nand_23_out, nand_24_out,
       nand_25_out, nand_26_out, nand_27_out, nand_28_out, nand_29_out, nand_30_out, nand_31_out,
       nand_32_out, nand_33_out, nand_34_out, nand_35_out, nand_36_out, nand_37_out, nand_38_out,
       nand_39_out, nand_40_out, nand_41_out, nand_42_out, nand_43_out, nand_44_out, nand_45_out,
       nand_46_out, nand_47_out, nand_48_out, nand_49_out, nand_50_out, nand_51_out, nand_52_out,
       nand_53_out, nand_54_out, nand_55_out, nand_56_out, nand_57_out, nand_58_out, nand_59_out,
       nand_60_out, nand_61_out, nand_62_out, nand_63_out, nand_64_out, nand_65_out, nand_66_out,
       nand_67_out, nand_68_out, shift_register_1_out, shift_register_2_out, xor_1_out;

  Shift_Register shift_register_1 (
    .in(in_3), .clk(clock_1_out), .out(shift_register_1_out));  // open: shift, load, clr, d0, q0, d1, q1, d2, q2, d3, q3, d4, q4, d5, q5, d6, q6, d7, q7
  Clock clock_1 (.out(clock_1_out));
  Shift_Register shift_register_2 (
    .in(in_4), .clk(clock_2_out), .out(shift_register_2_out));  // open: shift, load, clr, d0, q0, d1, q1, d2, q2, d3, q3, d4, q4, d5, q5, d6, q6, d7, q7
  Clock clock_2 (.out(clock_2_out));
  nand nand_1 (nand_1_out, in_1, in_2);
  nand nand_2 (nand_2_out, nand_1_out, nand_3_out);
  nand nand_3 (nand_3_out, nand_2_out, nand_4_out);
  nand nand_4 (nand_4_out, nand_1_out, in_2);
  D_Flip_Flop d_ff_1 (.clk(clock_1_out), .D(d_ff_1_qn), .Q(d_ff_1_q), .Qn(d_ff_1_qn));  // open: preset, en, reset
  D_Flip_Flop d_ff_2 (.clk(clock_2_out), .D(d_ff_2_qn), .Q(d_ff_2_q), .Qn(d_ff_2_qn));  // open: preset, en, reset
  nand nand_5 (nand_5_out, shift_register_1_out, d_ff_1_q);
  nand nand_6 (nand_6_out, nand_5_out, nand_7_out);
  nand nand_7 (nand_7_out, nand_6_out, nand_8_out);
  nand nand_8 (nand_8_out, nand_5_out, d_ff_1_q);
  xor xor_1 (xor_1_out, shift_register_2_out, d_ff_2_qn);
  LED led_1 (.in(nand_6_out));
  nand nand_9 (nand_9_out, nand_10_out, nand_12_out);
  nand nand_10 (nand_10_out, nand_6_out, d_ff_1_qn);
  nand nand_11 (nand_11_out, nand_10_out, d_ff_1_qn);
  nand nand_12 (nand_12_out, nand_9_out, nand_11_out);
  LED led_2 (.in(nand_13_out));
  nand nand_13 (nand_13_out, nand_14_out, nand_16_out);
  nand nand_14 (nand_14_out, xor_1_out, d_ff_2_q);
  nand nand_15 (nand_15_out, nand_14_out, d_ff_2_q);
  nand nand_16 (nand_16_out, nand_13_out, nand_15_out);
  LED led_3 (.in(nand_9_out));
  nand nand_17 (nand_17_out, nand_9_out, d_ff_1_q);
  nand nand_18 (nand_18_out, nand_17_out, nand_19_out);
  nand nand_19 (nand_19_out, nand_18_out, nand_20_out);
  nand nand_20 (nand_20_out, nand_17_out, d_ff_1_q);
  LED led_4 (.in(nand_22_out));
  nand nand_21 (nand_21_out, nand_13_out, d_ff_2_qn);
  nand nand_22 (nand_22_out, nand_21_out, nand_24_out);
  nand nand_23 (nand_23_out, nand_21_out, d_ff_2_qn);
  nand nand_24 (nand_24_out, nand_22_out, nand_23_out);
  LED led_5 (.in(nand_18_out));
  nand nand_25 (nand_25_out, nand_18_out, d_ff_1_qn);
  nand nand_26 (nand_26_out, nand_25_out, nand_28_out);
  nand nand_27 (nand_27_out, nand_25_out, d_ff_1_qn);
  nand nand_28 (nand_28_out, nand_26_out, nand_27_out);
  LED led_6 (.in(nand_30_out));
  nand nand_29 (nand_29_out, nand_22_out, d_ff_2_q);
  nand nand_30 (nand_30_out, nand_29_out, nand_31_out);
  nand nand_31 (nand_31_out, nand_30_out, nand_32_out);
  nand nand_32 (nand_32_out, nand_29_out, d_ff_2_q);
  LED led_7 (.in(nand_26_out));
  nand nand_33 (nand_33_out, nand_34_out, nand_35_out);
  nand nand_34 (nand_34_out, nand_26_out, d_ff_1_q);
  nand nand_35 (nand_35_out, nand_33_out, nand_36_out);
  nand nand_36 (nand_36_out, nand_34_out, d_ff_1_q);
  LED led_8 (.in(nand_37_out));
  nand nand_37 (nand_37_out, nand_38_out, nand_39_out);
  nand nand_38 (nand_38_out, nand_30_out, d_ff_2_qn);
  nand nand_39 (nand_39_out, nand_37_out, nand_40_out);
  nand nand_40 (nand_40_out, nand_38_out, d_ff_2_qn);
  LED led_9 (.in(nand_33_out));
  nand nand_41 (nand_41_out, nand_33_out, d_ff_1_qn);
  nand nand_42 (nand_42_out, nand_41_out, nand_43_out);
  nand nand_43 (nand_43_out, nand_42_out, nand_44_out);
  nand nand_44 (nand_44_out, nand_41_out, d_ff_1_qn);
  LED led_10 (.in(nand_45_out));
  nand nand_45 (nand_45_out, nand_46_out, nand_47_out);
  nand nand_46 (nand_46_out, nand_37_out, d_ff_2_q);
  nand nand_47 (nand_47_out, nand_45_out, nand_48_out);
  nand nand_48 (nand_48_out, nand_46_out, d_ff_2_q);
  LED led_11 (.in(nand_42_out));
  nand nand_49 (nand_49_out, nand_42_out, d_ff_1_q);
  nand nand_50 (nand_50_out, nand_49_out, nand_51_out);
  nand nand_51 (nand_51_out, nand_50_out, nand_52_out);
  nand nand_52 (nand_52_out, nand_49_out, d_ff_1_q);
  LED led_12 (.in(nand_53_out));
  nand nand_53 (nand_53_out, nand_54_out, nand_55_out);
  nand nand_54 (nand_54_out, nand_45_out, d_ff_2_qn);
  nand nand_55 (nand_55_out, nand_53_out, nand_56_out);
  nand nand_56 (nand_56_out, nand_54_out, d_ff_2_qn);
  LED led_13 (.in(nand_50_out));
  nand nand_57 (nand_57_out, nand_50_out, d_ff_1_qn);
  nand nand_58 (nand_58_out, nand_57_out, nand_59_out);
  nand nand_59 (nand_59_out, nand_58_out, nand_60_out);
  nand nand_60 (nand_60_out, nand_57_out, d_ff_1_qn);
  LED led_14 (.in(nand_62_out));
  nand nand_61 (nand_61_out, nand_53_out, d_ff_2_q);
  nand nand_62 (nand_62_out, nand_61_out, nand_64_out);
  nand nand_63 (nand_63_out, nand_61_out, d_ff_2_q);
  nand nand_64 (nand_64_out, nand_62_out, nand_63_out);
  LED led_15 (.in(nand_58_out));
  LED led_16 (.in(nand_66_out));
  nand nand_65 (nand_65_out, nand_62_out, d_ff_2_qn);
  nand nand_66 (nand_66_out, nand_65_out, nand_67_out);
  nand nand_67 (nand_67_out, nand_66_out, nand_68_out);
  nand nand_68 (nand_68_out, nand_65_out, d_ff_2_qn);
endmodule

module Grid (
  input  in_1,
  input  in_2,
  input  in_3,
  input  in_4,
  input  in_5,
  input  in_6,
  input  in_7,
  input  in_8,
  input  in_9,
  input  in_10,
  input  in_11
);

  wire and_1_out, clock_1_out, d_ff_1_q, d_ff_2_q, d_ff_3_q, d_ff_4_q, d_ff_5_q, d_ff_6_q, d_ff_7_q,
       d_ff_8_q, d_ff_9_q, d_ff_10_q, d_ff_11_q, d_ff_12_q, d_ff_13_q, d_ff_14_q, d_ff_15_q, d_ff_16_q,
       d_ff_17_q, d_ff_18_q, d_ff_19_q, d_ff_20_q, d_ff_21_q, d_ff_22_q, d_ff_23_q, d_ff_24_q, d_ff_25_q,
       nand_1_out, nand_2_out, nand_3_out, nand_4_out, nand_6_out, nand_7_out, nand_8_out, nand_10_out,
       nand_11_out, nand_12_out, nand_14_out, nand_15_out, nand_16_out, nand_17_out, nand_19_out,
       nand_20_out, nand_22_out, nand_23_out, nand_24_out, nand_26_out, nand_27_out, nand_28_out,
       nand_30_out, nand_31_out, nand_32_out, nand_34_out, nand_35_out, nand_36_out, nand_37_out,
       nand_39_out, nand_40_out, nand_42_out, nand_43_out, nand_44_out, nand_45_out, nand_47_out,
       nand_48_out, nand_49_out, nand_51_out, nand_52_out, nand_54_out, nand_55_out, nand_56_out,
       nand_58_out, nand_59_out, nand_60_out, nand_61_out, nand_63_out, nand_64_out, nand_66_out,
       nand_67_out, nand_68_out, nand_69_out, nand_70_out, nand_71_out, nand_72_out, nand_73_out,
       nand_74_out, nand_75_out, nand_76_out, nand_77_out, nand_78_out, nand_79_out, nand_80_out,
       nand_81_out, nand_82_out, nand_83_out, nand_84_out, nand_86_out, nand_88_out, nand_90_out,
       nand_92_out, nand_94_out, nand_96_out, nand_98_out, nand_100_out, nand_101_out, nand_103_out,
       nand_104_out, nand_106_out, nand_107_out, nand_108_out, nand_110_out, nand_111_out, nand_112_out,
       nand_114_out, nand_115_out, nand_116_out, nand_117_out, nand_119_out, nand_120_out, nand_122_out,
       nand_123_out, nand_124_out, nand_126_out, nand_127_out, nand_128_out, nand_129_out, nand_131_out,
       nand_132_out, nand_133_out, nand_135_out, nand_136_out, nand_137_out, nand_139_out, nand_140_out,
       nand_141_out, nand_143_out, nand_144_out, nand_145_out, nand_147_out, nand_148_out, nand_150_out,
       nand_151_out, nand_152_out, nand_154_out, nand_155_out, nand_156_out, nand_157_out, nand_159_out,
       nand_160_out, nand_162_out, nand_163_out, nand_164_out, nand_166_out, nand_167_out, nand_168_out,
       nand_170_out, nand_171_out, nand_172_out, nand_173_out, nand_175_out, nand_176_out, nand_177_out,
       nand_179_out, nand_180_out, nand_182_out, nand_183_out, nand_184_out, nand_186_out, nand_187_out,
       nand_188_out, nand_189_out, nand_191_out, nand_192_out, nand_193_out, nand_195_out, nand_196_out,
       nand_197_out, nand_198_out, nand_199_out, nand_200_out, nand_201_out, nand_202_out, nand_203_out,
       nand_204_out, nand_205_out, nand_206_out, nand_207_out, nand_208_out, nand_209_out, nand_210_out,
       nand_211_out, nand_212_out, nand_214_out, nand_216_out, nand_218_out, nand_220_out, nand_222_out,
       nand_224_out, nand_226_out, nand_228_out, nand_229_out, nand_231_out, nand_232_out, nand_234_out,
       nand_235_out, nand_236_out, nand_237_out, nand_239_out, nand_240_out, nand_241_out, nand_243_out,
       nand_244_out, nand_245_out, nand_247_out, nand_248_out, nand_249_out, nand_251_out, nand_252_out,
       nand_254_out, nand_255_out, nand_256_out, nand_257_out, nand_259_out, nand_260_out, nand_262_out,
       nand_263_out, nand_264_out, nand_265_out, nand_267_out, nand_268_out, nand_270_out, nand_271_out,
       nand_272_out, nand_273_out, nand_275_out, nand_276_out, nand_278_out, nand_279_out, nand_280_out,
       nand_282_out, nand_283_out, nand_284_out, nand_286_out, nand_287_out, nand_288_out, nand_290_out,
       nand_291_out, nand_292_out, shift_register_1_out, shift_register_2_out, shift_register_3_out,
       shift_register_4_out, shift_register_5_out, shift_register_6_out, shift_register_7_out,
       shift_register_8_out, undriven, undriven_2, undriven_3, undriven_4, undriven_5, undriven_6,
       undriven_7, undriven_8, undriven_9;
  wire [6:0] nand_130_out, nand_161_out;
  wire [7:0] nand_33_out, nand_65_out, nand_99_out, nand_194_out, nand_227_out, nand_258_out, nand_289_out;
  wire [7:7] nand_102_out, nand_134_out;

  nand nand_1 (nand_1_out, nand_2_out, nand_4_out);
  nand nand_2 (nand_2_out, in_1, in_2);
  nand nand_3 (nand_3_out, nand_2_out, in_2);
  nand nand_4 (nand_4_out, nand_1_out, nand_3_out);
  nand nand_5 (nand_33_out[7], nand_6_out, nand_7_out);
  nand nand_6 (nand_6_out, undriven_2, undriven);
  nand nand_7 (nand_7_out, nand_33_out[7], nand_8_out);
  nand nand_8 (nand_8_out, nand_6_out, undriven);
  nand nand_9 (nand_33_out[6], nand_10_out, nand_11_out);
  nand nand_10 (nand_10_out, undriven_3, undriven);
  nand nand_11 (nand_11_out, nand_33_out[6], nand_12_out);
  nand nand_12 (nand_12_out, nand_10_out, undriven);
  nand nand_13 (nand_33_out[5], nand_14_out, nand_15_out);
  nand nand_14 (nand_14_out, undriven_4, undriven);
  nand nand_15 (nand_15_out, nand_33_out[5], nand_16_out);
  nand nand_16 (nand_16_out, nand_14_out, undriven);
  nand nand_17 (nand_17_out, undriven_5, undriven);
  nand nand_18 (nand_33_out[4], nand_17_out, nand_19_out);
  nand nand_19 (nand_19_out, nand_33_out[4], nand_20_out);
  nand nand_20 (nand_20_out, nand_17_out, undriven);
  nand nand_21 (nand_33_out[3], nand_22_out, nand_24_out);
  nand nand_22 (nand_22_out, undriven_6, undriven);
  nand nand_23 (nand_23_out, nand_22_out, undriven);
  nand nand_24 (nand_24_out, nand_33_out[3], nand_23_out);
  nand nand_25 (nand_33_out[2], nand_26_out, nand_27_out);
  nand nand_26 (nand_26_out, undriven_7, undriven);
  nand nand_27 (nand_27_out, nand_33_out[2], nand_28_out);
  nand nand_28 (nand_28_out, nand_26_out, undriven);
  nand nand_29 (nand_33_out[1], nand_30_out, nand_31_out);
  nand nand_30 (nand_30_out, undriven_8, undriven);
  nand nand_31 (nand_31_out, nand_33_out[1], nand_32_out);
  nand nand_32 (nand_32_out, nand_30_out, undriven);
  nand nand_33 (nand_33_out[0], nand_34_out, nand_36_out);
  nand nand_34 (nand_34_out, undriven_9, undriven);
  nand nand_35 (nand_35_out, nand_34_out, undriven);
  nand nand_36 (nand_36_out, nand_33_out[0], nand_35_out);
  Clock clock_1 (.out(clock_1_out));
  Shift_Register shift_register_1 (
    .in(in_3), .clk(clock_1_out), .out(shift_register_1_out));  // open: shift, load, clr, d0, q0, d1, q1, d2, q2, d3, q3, d4, q4, d5, q5, d6, q6, d7, q7
  Shift_Register shift_register_2 (
    .in(in_4), .clk(clock_1_out), .out(shift_register_2_out));  // open: shift, load, clr, d0, q0, d1, q1, d2, q2, d3, q3, d4, q4, d5, q5, d6, q6, d7, q7
  Shift_Register shift_register_3 (
    .in(in_5), .clk(clock_1_out), .out(shift_register_3_out));  // open: shift, load, clr, d0, q0, d1, q1, d2, q2, d3, q3, d4, q4, d5, q5, d6, q6, d7, q7
  Shift_Register shift_register_4 (
    .in(in_6), .clk(clock_1_out), .out(shift_register_4_out));  // open: shift, load, clr, d0, q0, d1, q1, d2, q2, d3, q3, d4, q4, d5, q5, d6, q6, d7, q7
  Shift_Register shift_register_5 (
    .in(in_7), .clk(clock_1_out), .out(shift_register_5_out));  // open: shift, load, clr, d0, q0, d1, q1, d2, q2, d3, q3, d4, q4, d5, q5, d6, q6, d7, q7
  Shift_Register shift_register_6 (
    .in(in_8), .clk(clock_1_out), .out(shift_register_6_out));  // open: shift, load, clr, d0, q0, d1, q1, d2, q2, d3, q3, d4, q4, d5, q5, d6, q6, d7, q7
  Shift_Register shift_register_7 (
    .in(in_9), .clk(clock_1_out), .out(shift_register_7_out));  // open: shift, load, clr, d0, q0, d1, q1, d2, q2, d3, q3, d4, q4, d5, q5, d6, q6, d7, q7
  Shift_Register shift_register_8 (
    .in(in_10), .clk(clock_1_out), .out(shift_register_8_out));  // open: shift, load, clr, d0, q0, d1, q1, d2, q2, d3, q3, d4, q4, d5, q5, d6, q6, d7, q7
  and and_1 (and_1_out, in_11, d_ff_25_q);
  D_Flip_Flop d_ff_1 (.clk(clock_1_out), .D(and_1_out), .Q(d_ff_1_q));  // open: Qn, preset, en, reset
  D_Flip_Flop d_ff_2 (.clk(clock_1_out), .D(shift_register_1_out), .Q(d_ff_2_q));  // open: Qn, preset, en, reset
  D_Flip_Flop d_ff_3 (.clk(clock_1_out), .D(shift_register_2_out), .Q(d_ff_3_q));  // open: Qn, preset, en, reset
  D_Flip_Flop d_ff_4 (.clk(clock_1_out), .D(shift_register_3_out), .Q(d_ff_4_q));  // open: Qn, preset, en, reset
  D_Flip_Flop d_ff_5 (.clk(clock_1_out), .D(shift_register_4_out), .Q(d_ff_5_q));  // open: Qn, preset, en, reset
  D_Flip_Flop d_ff_6 (.clk(clock_1_out), .D(shift_register_5_out), .Q(d_ff_6_q));  // open: Qn, preset, en, reset
  D_Flip_Flop d_ff_7 (.clk(clock_1_out), .D(shift_register_6_out), .Q(d_ff_7_q));  // open: Qn, preset, en, reset
  D_Flip_Flop d_ff_8 (.clk(clock_1_out), .D(shift_register_7_out), .Q(d_ff_8_q));  // open: Qn, preset, en, reset
  D_Flip_Flop d_ff_9 (.clk(clock_1_out), .D(shift_register_8_out), .Q(d_ff_9_q));  // open: Qn, preset, en, reset
  D_Flip_Flop #(.trigger("falling")) d_ff_10 (
    .clk(clock_1_out), .D(d_ff_2_q), .Q(d_ff_10_q));  // open: Qn, preset, en, reset
  D_Flip_Flop #(.trigger("falling")) d_ff_11 (
    .clk(clock_1_out), .D(d_ff_3_q), .Q(d_ff_11_q));  // open: Qn, preset, en, reset
  D_Flip_Flop #(.trigger("falling")) d_ff_12 (
    .clk(clock_1_out), .D(d_ff_4_q), .Q(d_ff_12_q));  // open: Qn, preset, en, reset
  D_Flip_Flop #(.trigger("falling")) d_ff_13 (
    .clk(clock_1_out), .D(d_ff_5_q), .Q(d_ff_13_q));  // open: Qn, preset, en, reset
  D_Flip_Flop #(.trigger("falling")) d_ff_14 (
    .clk(clock_1_out), .D(d_ff_6_q), .Q(d_ff_14_q));  // open: Qn, preset, en, reset
  D_Flip_Flop #(.trigger("falling")) d_ff_15 (
    .clk(clock_1_out), .D(d_ff_7_q), .Q(d_ff_15_q));  // open: Qn, preset, en, reset
  D_Flip_Flop #(.trigger("falling")) d_ff_16 (
    .clk(clock_1_out), .D(d_ff_8_q), .Q(d_ff_16_q));  // open: Qn, preset, en, reset
  D_Flip_Flop #(.trigger("falling")) d_ff_17 (
    .clk(clock_1_out), .D(d_ff_9_q), .Q(d_ff_17_q));  // open: Qn, preset, en, reset
  D_Flip_Flop d_ff_18 (.clk(clock_1_out), .D(d_ff_1_q), .Q(d_ff_18_q));  // open: Qn, preset, en, reset
  nand nand_37 (nand_37_out, d_ff_10_q, d_ff_18_q);
  nand nand_38 (nand_65_out[7], nand_37_out, nand_40_out);
  nand nand_39 (nand_39_out, nand_37_out, d_ff_18_q);
  nand nand_40 (nand_40_out, nand_65_out[7], nand_39_out);
  nand nand_41 (nand_65_out[6], nand_42_out, nand_44_out);
  nand nand_42 (nand_42_out, d_ff_11_q, d_ff_18_q);
  nand nand_43 (nand_43_out, nand_42_out, d_ff_18_q);
  nand nand_44 (nand_44_out, nand_65_out[6], nand_43_out);
  nand nand_45 (nand_45_out, d_ff_12_q, d_ff_18_q);
  nand nand_46 (nand_65_out[5], nand_45_out, nand_47_out);
  nand nand_47 (nand_47_out, nand_65_out[5], nand_48_out);
  nand nand_48 (nand_48_out, nand_45_out, d_ff_18_q);
  nand nand_49 (nand_49_out, d_ff_13_q, d_ff_18_q);
  nand nand_50 (nand_65_out[4], nand_49_out, nand_51_out);
  nand nand_51 (nand_51_out, nand_65_out[4], nand_52_out);
  nand nand_52 (nand_52_out, nand_49_out, d_ff_18_q);
  nand nand_53 (nand_65_out[3], nand_54_out, nand_55_out);
  nand nand_54 (nand_54_out, d_ff_14_q, d_ff_18_q);
  nand nand_55 (nand_55_out, nand_65_out[3], nand_56_out);
  nand nand_56 (nand_56_out, nand_54_out, d_ff_18_q);
  nand nand_57 (nand_65_out[2], nand_58_out, nand_59_out);
  nand nand_58 (nand_58_out, d_ff_15_q, d_ff_18_q);
  nand nand_59 (nand_59_out, nand_65_out[2], nand_60_out);
  nand nand_60 (nand_60_out, nand_58_out, d_ff_18_q);
  nand nand_61 (nand_61_out, d_ff_16_q, d_ff_18_q);
  nand nand_62 (nand_65_out[1], nand_61_out, nand_63_out);
  nand nand_63 (nand_63_out, nand_65_out[1], nand_64_out);
  nand nand_64 (nand_64_out, nand_61_out, d_ff_18_q);
  nand nand_65 (nand_65_out[0], nand_66_out, nand_67_out);
  nand nand_66 (nand_66_out, d_ff_17_q, d_ff_18_q);
  nand nand_67 (nand_67_out, nand_65_out[0], nand_68_out);
  nand nand_68 (nand_68_out, nand_66_out, d_ff_18_q);
  nand nand_69 (nand_69_out, d_ff_10_q, d_ff_19_q);
  nand nand_70 (nand_70_out, nand_69_out, d_ff_19_q);
  nand nand_71 (nand_71_out, d_ff_11_q, d_ff_19_q);
  nand nand_72 (nand_72_out, nand_71_out, d_ff_19_q);
  nand nand_73 (nand_73_out, d_ff_12_q, d_ff_19_q);
  nand nand_74 (nand_74_out, nand_73_out, d_ff_19_q);
  nand nand_75 (nand_75_out, d_ff_13_q, d_ff_19_q);
  nand nand_76 (nand_76_out, nand_75_out, d_ff_19_q);
  nand nand_77 (nand_77_out, d_ff_14_q, d_ff_19_q);
  nand nand_78 (nand_78_out, nand_77_out, d_ff_19_q);
  nand nand_79 (nand_79_out, d_ff_15_q, d_ff_19_q);
  nand nand_80 (nand_80_out, nand_79_out, d_ff_19_q);
  nand nand_81 (nand_81_out, d_ff_16_q, d_ff_19_q);
  nand nand_82 (nand_82_out, nand_81_out, d_ff_19_q);
  nand nand_83 (nand_83_out, d_ff_17_q, d_ff_19_q);
  nand nand_84 (nand_84_out, nand_83_out, d_ff_19_q);
  D_Flip_Flop d_ff_19 (.clk(clock_1_out), .D(d_ff_18_q), .Q(d_ff_19_q));  // open: Qn, preset, en, reset
  nand nand_85 (nand_99_out[7], nand_69_out, nand_86_out);
  nand nand_86 (nand_86_out, nand_99_out[7], nand_70_out);
  nand nand_87 (nand_99_out[6], nand_71_out, nand_88_out);
  nand nand_88 (nand_88_out, nand_99_out[6], nand_72_out);
  nand nand_89 (nand_99_out[5], nand_73_out, nand_90_out);
  nand nand_90 (nand_90_out, nand_99_out[5], nand_74_out);
  nand nand_91 (nand_99_out[4], nand_75_out, nand_92_out);
  nand nand_92 (nand_92_out, nand_99_out[4], nand_76_out);
  nand nand_93 (nand_99_out[3], nand_77_out, nand_94_out);
  nand nand_94 (nand_94_out, nand_99_out[3], nand_78_out);
  nand nand_95 (nand_99_out[2], nand_79_out, nand_96_out);
  nand nand_96 (nand_96_out, nand_99_out[2], nand_80_out);
  nand nand_97 (nand_99_out[1], nand_81_out, nand_98_out);
  nand nand_98 (nand_98_out, nand_99_out[1], nand_82_out);
  nand nand_99 (nand_99_out[0], nand_83_out, nand_100_out);
  nand nand_100 (nand_100_out, nand_99_out[0], nand_84_out);
  D_Flip_Flop d_ff_20 (.clk(clock_1_out), .D(d_ff_19_q), .Q(d_ff_20_q));  // open: Qn, preset, en, reset
  nand nand_101 (nand_101_out, d_ff_10_q, d_ff_20_q);
  nand nand_102 (nand_102_out[7], nand_101_out, nand_103_out);
  nand nand_103 (nand_103_out, nand_102_out[7], nand_104_out);
  nand nand_104 (nand_104_out, nand_101_out, d_ff_20_q);
  nand nand_105 (nand_130_out[6], nand_106_out, nand_108_out);
  nand nand_106 (nand_106_out, d_ff_11_q, d_ff_20_q);
  nand nand_107 (nand_107_out, nand_106_out, d_ff_20_q);
  nand nand_108 (nand_108_out, nand_130_out[6], nand_107_out);
  nand nand_109 (nand_130_out[5], nand_110_out, nand_112_out);
  nand nand_110 (nand_110_out, d_ff_12_q, d_ff_20_q);
  nand nand_111 (nand_111_out, nand_110_out, d_ff_20_q);
  nand nand_112 (nand_112_out, nand_130_out[5], nand_111_out);
  nand nand_113 (nand_130_out[4], nand_114_out, nand_116_out);
  nand nand_114 (nand_114_out, d_ff_13_q, d_ff_20_q);
  nand nand_115 (nand_115_out, nand_114_out, d_ff_20_q);
  nand nand_116 (nand_116_out, nand_130_out[4], nand_115_out);
  nand nand_117 (nand_117_out, d_ff_14_q, d_ff_20_q);
  nand nand_118 (nand_130_out[3], nand_117_out, nand_120_out);
  nand nand_119 (nand_119_out, nand_117_out, d_ff_20_q);
  nand nand_120 (nand_120_out, nand_130_out[3], nand_119_out);
  nand nand_121 (nand_130_out[2], nand_122_out, nand_124_out);
  nand nand_122 (nand_122_out, d_ff_15_q, d_ff_20_q);
  nand nand_123 (nand_123_out, nand_122_out, d_ff_20_q);
  nand nand_124 (nand_124_out, nand_130_out[2], nand_123_out);
  nand nand_125 (nand_130_out[1], nand_126_out, nand_128_out);
  nand nand_126 (nand_126_out, d_ff_16_q, d_ff_20_q);
  nand nand_127 (nand_127_out, nand_126_out, d_ff_20_q);
  nand nand_128 (nand_128_out, nand_130_out[1], nand_127_out);
  nand nand_129 (nand_129_out, d_ff_17_q, d_ff_20_q);
  nand nand_130 (nand_130_out[0], nand_129_out, nand_132_out);
  nand nand_131 (nand_131_out, nand_129_out, d_ff_20_q);
  nand nand_132 (nand_132_out, nand_130_out[0], nand_131_out);
  D_Flip_Flop d_ff_21 (.clk(clock_1_out), .D(d_ff_20_q), .Q(d_ff_21_q));  // open: Qn, preset, en, reset
  nand nand_133 (nand_133_out, d_ff_10_q, d_ff_21_q);
  nand nand_134 (nand_134_out[7], nand_133_out, nand_135_out);
  nand nand_135 (nand_135_out, nand_134_out[7], nand_136_out);
  nand nand_136 (nand_136_out, nand_133_out, d_ff_21_q);
  nand nand_137 (nand_137_out, d_ff_11_q, d_ff_21_q);
  nand nand_138 (nand_161_out[6], nand_137_out, nand_140_out);
  nand nand_139 (nand_139_out, nand_137_out, d_ff_21_q);
  nand nand_140 (nand_140_out, nand_161_out[6], nand_139_out);
  nand nand_141 (nand_141_out, d_ff_12_q, d_ff_21_q);
  nand nand_142 (nand_161_out[5], nand_141_out, nand_143_out);
  nand nand_143 (nand_143_out, nand_161_out[5], nand_144_out);
  nand nand_144 (nand_144_out, nand_141_out, d_ff_21_q);
  nand nand_145 (nand_145_out, d_ff_13_q, d_ff_21_q);
  nand nand_146 (nand_161_out[4], nand_145_out, nand_148_out);
  nand nand_147 (nand_147_out, nand_145_out, d_ff_21_q);
  nand nand_148 (nand_148_out, nand_161_out[4], nand_147_out);
  nand nand_149 (nand_161_out[3], nand_150_out, nand_151_out);
  nand nand_150 (nand_150_out, d_ff_14_q, d_ff_21_q);
  nand nand_151 (nand_151_out, nand_161_out[3], nand_152_out);
  nand nand_152 (nand_152_out, nand_150_out, d_ff_21_q);
  nand nand_153 (nand_161_out[2], nand_154_out, nand_156_out);
  nand nand_154 (nand_154_out, d_ff_15_q, d_ff_21_q);
  nand nand_155 (nand_155_out, nand_154_out, d_ff_21_q);
  nand nand_156 (nand_156_out, nand_161_out[2], nand_155_out);
  nand nand_157 (nand_157_out, d_ff_16_q, d_ff_21_q);
  nand nand_158 (nand_161_out[1], nand_157_out, nand_160_out);
  nand nand_159 (nand_159_out, nand_157_out, d_ff_21_q);
  nand nand_160 (nand_160_out, nand_161_out[1], nand_159_out);
  nand nand_161 (nand_161_out[0], nand_162_out, nand_163_out);
  nand nand_162 (nand_162_out, d_ff_17_q, d_ff_21_q);
  nand nand_163 (nand_163_out, nand_161_out[0], nand_164_out);
  nand nand_164 (nand_164_out, nand_162_out, d_ff_21_q);
  D_Flip_Flop d_ff_22 (.clk(clock_1_out), .D(d_ff_21_q), .Q(d_ff_22_q));  // open: Qn, preset, en, reset
  DotMatrix #(.matrixcols(8), .matrixrows(8)) dotmatrix_1 (
    .col0(nand_65_out), .col1(nand_99_out), .col2({nand_102_out[7], nand_130_out}),
    .col3({nand_134_out[7], nand_161_out}), .col4(nand_194_out), .col5(nand_227_out), .col6(nand_258_out),
    .col7(nand_289_out));
  nand nand_165 (nand_194_out[7], nand_166_out, nand_167_out);
  nand nand_166 (nand_166_out, d_ff_10_q, d_ff_22_q);
  nand nand_167 (nand_167_out, nand_194_out[7], nand_168_out);
  nand nand_168 (nand_168_out, nand_166_out, d_ff_22_q);
  nand nand_169 (nand_194_out[6], nand_170_out, nand_171_out);
  nand nand_170 (nand_170_out, d_ff_11_q, d_ff_22_q);
  nand nand_171 (nand_171_out, nand_194_out[6], nand_172_out);
  nand nand_172 (nand_172_out, nand_170_out, d_ff_22_q);
  nand nand_173 (nand_173_out, d_ff_12_q, d_ff_22_q);
  nand nand_174 (nand_194_out[5], nand_173_out, nand_175_out);
  nand nand_175 (nand_175_out, nand_194_out[5], nand_176_out);
  nand nand_176 (nand_176_out, nand_173_out, d_ff_22_q);
  nand nand_177 (nand_177_out, d_ff_13_q, d_ff_22_q);
  nand nand_178 (nand_194_out[4], nand_177_out, nand_179_out);
  nand nand_179 (nand_179_out, nand_194_out[4], nand_180_out);
  nand nand_180 (nand_180_out, nand_177_out, d_ff_22_q);
  nand nand_181 (nand_194_out[3], nand_182_out, nand_184_out);
  nand nand_182 (nand_182_out, d_ff_14_q, d_ff_22_q);
  nand nand_183 (nand_183_out, nand_182_out, d_ff_22_q);
  nand nand_184 (nand_184_out, nand_194_out[3], nand_183_out);
  nand nand_185 (nand_194_out[2], nand_186_out, nand_188_out);
  nand nand_186 (nand_186_out, d_ff_15_q, d_ff_22_q);
  nand nand_187 (nand_187_out, nand_186_out, d_ff_22_q);
  nand nand_188 (nand_188_out, nand_194_out[2], nand_187_out);
  nand nand_189 (nand_189_out, d_ff_16_q, d_ff_22_q);
  nand nand_190 (nand_194_out[1], nand_189_out, nand_191_out);
  nand nand_191 (nand_191_out, nand_194_out[1], nand_192_out);
  nand nand_192 (nand_192_out, nand_189_out, d_ff_22_q);
  nand nand_193 (nand_193_out, d_ff_17_q, d_ff_22_q);
  nand nand_194 (nand_194_out[0], nand_193_out, nand_195_out);
  nand nand_195 (nand_195_out, nand_194_out[0], nand_196_out);
  nand nand_196 (nand_196_out, nand_193_out, d_ff_22_q);
  nand nand_197 (nand_197_out, d_ff_10_q, d_ff_23_q);
  nand nand_198 (nand_198_out, nand_197_out, d_ff_23_q);
  nand nand_199 (nand_199_out, d_ff_11_q, d_ff_23_q);
  nand nand_200 (nand_200_out, nand_199_out, d_ff_23_q);
  nand nand_201 (nand_201_out, d_ff_12_q, d_ff_23_q);
  nand nand_202 (nand_202_out, nand_201_out, d_ff_23_q);
  nand nand_203 (nand_203_out, d_ff_13_q, d_ff_23_q);
  nand nand_204 (nand_204_out, nand_203_out, d_ff_23_q);
  nand nand_205 (nand_205_out, d_ff_14_q, d_ff_23_q);
  nand nand_206 (nand_206_out, nand_205_out, d_ff_23_q);
  nand nand_207 (nand_207_out, d_ff_15_q, d_ff_23_q);
  nand nand_208 (nand_208_out, nand_207_out, d_ff_23_q);
  nand nand_209 (nand_209_out, d_ff_16_q, d_ff_23_q);
  nand nand_210 (nand_210_out, nand_209_out, d_ff_23_q);
  nand nand_211 (nand_211_out, d_ff_17_q, d_ff_23_q);
  nand nand_212 (nand_212_out, nand_211_out, d_ff_23_q);
  D_Flip_Flop d_ff_23 (.clk(clock_1_out), .D(d_ff_22_q), .Q(d_ff_23_q));  // open: Qn, preset, en, reset
  nand nand_213 (nand_227_out[7], nand_197_out, nand_214_out);
  nand nand_214 (nand_214_out, nand_227_out[7], nand_198_out);
  nand nand_215 (nand_227_out[6], nand_199_out, nand_216_out);
  nand nand_216 (nand_216_out, nand_227_out[6], nand_200_out);
  nand nand_217 (nand_227_out[5], nand_201_out, nand_218_out);
  nand nand_218 (nand_218_out, nand_227_out[5], nand_202_out);
  nand nand_219 (nand_227_out[4], nand_203_out, nand_220_out);
  nand nand_220 (nand_220_out, nand_227_out[4], nand_204_out);
  nand nand_221 (nand_227_out[3], nand_205_out, nand_222_out);
  nand nand_222 (nand_222_out, nand_227_out[3], nand_206_out);
  nand nand_223 (nand_227_out[2], nand_207_out, nand_224_out);
  nand nand_224 (nand_224_out, nand_227_out[2], nand_208_out);
  nand nand_225 (nand_227_out[1], nand_209_out, nand_226_out);
  nand nand_226 (nand_226_out, nand_227_out[1], nand_210_out);
  nand nand_227 (nand_227_out[0], nand_211_out, nand_228_out);
  nand nand_228 (nand_228_out, nand_227_out[0], nand_212_out);
  D_Flip_Flop d_ff_24 (.clk(clock_1_out), .D(d_ff_23_q), .Q(d_ff_24_q));  // open: Qn, preset, en, reset
  nand nand_229 (nand_229_out, d_ff_10_q, d_ff_24_q);
  nand nand_230 (nand_258_out[7], nand_229_out, nand_232_out);
  nand nand_231 (nand_231_out, nand_229_out, d_ff_24_q);
  nand nand_232 (nand_232_out, nand_258_out[7], nand_231_out);
  nand nand_233 (nand_258_out[6], nand_234_out, nand_235_out);
  nand nand_234 (nand_234_out, d_ff_11_q, d_ff_24_q);
  nand nand_235 (nand_235_out, nand_258_out[6], nand_236_out);
  nand nand_236 (nand_236_out, nand_234_out, d_ff_24_q);
  nand nand_237 (nand_237_out, d_ff_12_q, d_ff_24_q);
  nand nand_238 (nand_258_out[5], nand_237_out, nand_239_out);
  nand nand_239 (nand_239_out, nand_258_out[5], nand_240_out);
  nand nand_240 (nand_240_out, nand_237_out, d_ff_24_q);
  nand nand_241 (nand_241_out, d_ff_13_q, d_ff_24_q);
  nand nand_242 (nand_258_out[4], nand_241_out, nand_244_out);
  nand nand_243 (nand_243_out, nand_241_out, d_ff_24_q);
  nand nand_244 (nand_244_out, nand_258_out[4], nand_243_out);
  nand nand_245 (nand_245_out, d_ff_14_q, d_ff_24_q);
  nand nand_246 (nand_258_out[3], nand_245_out, nand_247_out);
  nand nand_247 (nand_247_out, nand_258_out[3], nand_248_out);
  nand nand_248 (nand_248_out, nand_245_out, d_ff_24_q);
  nand nand_249 (nand_249_out, d_ff_15_q, d_ff_24_q);
  nand nand_250 (nand_258_out[2], nand_249_out, nand_251_out);
  nand nand_251 (nand_251_out, nand_258_out[2], nand_252_out);
  nand nand_252 (nand_252_out, nand_249_out, d_ff_24_q);
  nand nand_253 (nand_258_out[1], nand_254_out, nand_256_out);
  nand nand_254 (nand_254_out, d_ff_16_q, d_ff_24_q);
  nand nand_255 (nand_255_out, nand_254_out, d_ff_24_q);
  nand nand_256 (nand_256_out, nand_258_out[1], nand_255_out);
  nand nand_257 (nand_257_out, d_ff_17_q, d_ff_24_q);
  nand nand_258 (nand_258_out[0], nand_257_out, nand_259_out);
  nand nand_259 (nand_259_out, nand_258_out[0], nand_260_out);
  nand nand_260 (nand_260_out, nand_257_out, d_ff_24_q);
  D_Flip_Flop d_ff_25 (.clk(clock_1_out), .D(d_ff_24_q), .Q(d_ff_25_q));  // open: Qn, preset, en, reset
  nand nand_261 (nand_289_out[7], nand_262_out, nand_263_out);
  nand nand_262 (nand_262_out, d_ff_10_q, d_ff_25_q);
  nand nand_263 (nand_263_out, nand_289_out[7], nand_264_out);
  nand nand_264 (nand_264_out, nand_262_out, d_ff_25_q);
  nand nand_265 (nand_265_out, d_ff_11_q, d_ff_25_q);
  nand nand_266 (nand_289_out[6], nand_265_out, nand_268_out);
  nand nand_267 (nand_267_out, nand_265_out, d_ff_25_q);
  nand nand_268 (nand_268_out, nand_289_out[6], nand_267_out);
  nand nand_269 (nand_289_out[5], nand_270_out, nand_272_out);
  nand nand_270 (nand_270_out, d_ff_12_q, d_ff_25_q);
  nand nand_271 (nand_271_out, nand_270_out, d_ff_25_q);
  nand nand_272 (nand_272_out, nand_289_out[5], nand_271_out);
  nand nand_273 (nand_273_out, d_ff_13_q, d_ff_25_q);
  nand nand_274 (nand_289_out[4], nand_273_out, nand_276_out);
  nand nand_275 (nand_275_out, nand_273_out, d_ff_25_q);
  nand nand_276 (nand_276_out, nand_289_out[4], nand_275_out);
  nand nand_277 (nand_289_out[3], nand_278_out, nand_280_out);
  nand nand_278 (nand_278_out, d_ff_14_q, d_ff_25_q);
  nand nand_279 (nand_279_out, nand_278_out, d_ff_25_q);
  nand nand_280 (nand_280_out, nand_289_out[3], nand_279_out);
  nand nand_281 (nand_289_out[2], nand_282_out, nand_284_out);
  nand nand_282 (nand_282_out, d_ff_15_q, d_ff_25_q);
  nand nand_283 (nand_283_out, nand_282_out, d_ff_25_q);
  nand nand_284 (nand_284_out, nand_289_out[2], nand_283_out);
  nand nand_285 (nand_289_out[1], nand_286_out, nand_287_out);
  nand nand_286 (nand_286_out, d_ff_16_q, d_ff_25_q);
  nand nand_287 (nand_287_out, nand_289_out[1], nand_288_out);
  nand nand_288 (nand_288_out, nand_286_out, d_ff_25_q);
  nand nand_289 (nand_289_out[0], nand_290_out, nand_291_out);
  nand nand_290 (nand_290_out, d_ff_17_q, d_ff_25_q);
  nand nand_291 (nand_291_out, nand_289_out[0], nand_292_out);
  nand nand_292 (nand_292_out, nand_290_out, d_ff_25_q);
endmodule
